// Logisim project multitest.circ as structural Verilog: 1 circuit, main circuit main
module main (
);

  wire and_1_out, and_2_out, and_3_out, and_4_out, CLK, clock_1_out, f1, f2, not_1_out, not_2_out, not_3_out,
       not_4_out, Reset_out, X1, X2, X3, X4;
  wire [4:4] counter_1_q;

  not not_1 (not_1_out, X1);
  not not_2 (not_2_out, X2);
  not not_3 (not_3_out, X4);
  and and_1 (and_1_out, not_1_out, not_2_out, X4);
  and and_2 (and_2_out, X2, X3, not_1_out, not_3_out);
  and and_3 (and_3_out, X1, X4);
  and and_4 (and_4_out, X2, X4);
  or or_1 (f2, and_1_out, and_2_out, and_3_out);
  or or_2 (f1, and_1_out, and_4_out, and_2_out);
  // Probe on {counter_1_q[4], X4, X3, X2, X1}
  Counter #(.width(5), .max('h10), .ongoal("stay")) counter_1 (
    .Q({counter_1_q[4], X4, X3, X2, X1}), .clk(CLK), .clr(Reset_out));  // open: load, D, count, carry
  TTY #(.rows(1), .cols(16)) tty_1 (.data({5'b01100, f2, f1}), .clk(CLK), .clr(Reset_out));  // open: we
  not not_4 (not_4_out, counter_1_q[4]);
  Clock clock_1 (.out(clock_1_out));
  and and_5 (CLK, not_4_out, clock_1_out);
  Button Reset (.out(Reset_out));

  // Notes on the sheet:
  //   Press Reset button, then Ctrl-k or Ctrl-t
  //   Please set tick frequency to 2KHz
  //   0000003032133213
endmodule
