// Logisim project alutest.circ as structural Verilog: 2 circuits, main circuit main
module main (
);

  wire A0, A1, A2, A3, A4, B0, B1, B2, B3, B4, C0, C1, C2, C3, C4, C5, CIN, clock_1_out, clock_2_out, D0, D1,
       D2, D3, go, HCLK, not_1_out, reset, S0, S1;
  wire [2:0] multiplexer_1_out;
  wire [6:1] counter_1_q;

  alu alu_1 (.A(A0), .B(B0), .Cin(CIN), .in_4({S1, S0}), .out_5(C0), .out_6(D0));
  alu alu_2 (.A(A1), .B(B1), .Cin(D0), .in_4({S1, S0}), .out_5(C1), .out_6(D1));
  alu alu_3 (.A(A2), .B(B2), .Cin(D1), .in_4({S1, S0}), .out_5(C2), .out_6(D2));
  alu alu_4 (.A(A3), .B(B3), .Cin(D2), .in_4({S1, S0}), .out_5(C3), .out_6(D3));
  alu alu_5 (.A(A4), .B(B4), .Cin(D3), .in_4({S1, S0}), .out_5(C4), .out_6(C5));
  // Probe on {C5, C4, C3}
  // Probe on {C2, C1, C0}
  Multiplexer #(.width(3)) multiplexer_1 (
    .in0({C5, C4, C3}), .in1({C2, C1, C0}), .out(multiplexer_1_out), .sel(HCLK));  // open: en
  // Probe on multiplexer_1_out
  // Probe on {4'b0110, multiplexer_1_out}
  TTY #(.rows(32), .cols(2)) tty_1 (.data({4'b0110, multiplexer_1_out}), .clk(clock_1_out), .we(go), .clr(reset));
  Clock clock_1 (.out(clock_1_out));
  // Probe on {A4, A3, A2, A1, A0, CIN}
  // Probe on {B4, B3, B2, B1, B0}
  // Probe on S1
  Counter #(.width(7), .max('h7f), .ongoal("stay")) counter_1 (
    .Q({counter_1_q, HCLK}), .clk(clock_2_out), .clr(reset));  // open: load, D, count, carry
  Clock clock_2 (.out(clock_2_out));
  // Probe on S0
  not not_1 (not_1_out, HCLK);
  Button u_Reset (.out(reset));
  Random #(.width(13), .seed(34573)) random_1 (
    .clk(not_1_out), .next(go), .out({B4, B3, B2, B1, B0, A4, A3, A2, A1, A0, CIN, S1, S0}), .clr(reset));
  not not_2 (go, counter_1_q[6]);

  // Notes on the sheet:
  //   07
  //   51
  //   40
  //   51
  //   77
  //   77
  //   57
  //   63
  //   43
  //   77
  //   60
  //   51
  //   46
  //   71
  //   32
  //   43
  //   34
  //   50
  //   53
  //   00
  //   07
  //   02
  //   74
  //   04
  //   35
  //   52
  //   52
  //   50
  //   65
  //   46
  //   11
  //   57
endmodule

module alu (
  input  A,
  input  B,
  input  Cin,
  input  [1:0] in_4,
  output out_5,
  output out_6
);

  wire and_1_out, and_2_out, and_3_out, and_4_out, and_5_out, and_6_out, and_7_out, not_1_out, not_2_out,
       not_3_out, or_1_out, or_2_out, or_3_out;

  and and_1 (and_1_out, A, B);
  and and_2 (and_2_out, A, B);
  not not_1 (not_1_out, and_1_out);
  or or_1 (or_1_out, A, B);
  and and_3 (and_3_out, not_1_out, or_1_out);
  not not_2 (not_2_out, A);
  and and_4 (and_4_out, and_3_out, Cin);
  not not_3 (not_3_out, and_5_out);
  and and_5 (and_5_out, and_3_out, Cin);
  or or_2 (or_2_out, Cin, and_3_out);
  and and_6 (and_6_out, A, B);
  or or_3 (or_3_out, A, B);
  or or_4 (out_6, and_4_out, and_2_out);
  and and_7 (and_7_out, not_3_out, or_2_out);
  Multiplexer #(.select(2)) multiplexer_1 (
    .in0(and_6_out), .in1(or_3_out), .in2(not_2_out), .in3(and_7_out), .out(out_5), .sel(in_4));  // open: en
endmodule
