// Logisim project secdedtest.circ as structural Verilog: 1 circuit, main circuit main
module main (
);

  wire C0, C0_prime, C1, C1_prime, C2, C2_prime, C3, C3_prime, C5, CLK, clock_1_out, D0, D1, D2, D3, D4, D5,
       D6, D7, D8, D9, decoder_1_out0, decoder_1_out1, decoder_1_out2, decoder_1_out3, decoder_1_out4,
       decoder_1_out5, decoder_1_out6, decoder_1_out7, decoder_1_out8, decoder_1_out9, decoder_1_out10,
       decoder_1_out11, decoder_1_out12, decoder_1_out13, decoder_1_out14, decoder_1_out15, E, go, reset, Z0,
       Z1, Z2, Z3, Z4, Z5, Z6, Z7, Z8, Z9;
  wire [3:0] multiplexer_1_out, odd_parity_1_out;
  wire [5:0] counter_1_q;

  xor odd_parity_1 (odd_parity_1_out[0], D0, C0, D1, D3, D4, D6, D8);
  xor odd_parity_2 (odd_parity_1_out[1], C1, D0, D2, D3, D5, D6, D9);
  xor odd_parity_3 (odd_parity_1_out[2], C2, D1, D2, D3, D7, D8, D9);
  xor odd_parity_4 (odd_parity_1_out[3], C3, D4, D5, D6, D7, D8, D9);
  xor odd_parity_5 (E, C0_prime, C1_prime, Z0, Z1, Z2, Z3, Z4, Z5, Z6, Z7, Z8, C5, Z9, C2_prime, C3_prime);
  Decoder #(.select(4)) decoder_1 (
    .out0(decoder_1_out0), .out1(decoder_1_out1), .out2(decoder_1_out2), .out3(decoder_1_out3),
    .out4(decoder_1_out4), .out5(decoder_1_out5), .out6(decoder_1_out6), .out7(decoder_1_out7),
    .out8(decoder_1_out8), .out9(decoder_1_out9), .out10(decoder_1_out10), .out11(decoder_1_out11),
    .out12(decoder_1_out12), .out13(decoder_1_out13), .out14(decoder_1_out14), .out15(decoder_1_out15),
    .sel(odd_parity_1_out));  // open: en
  xor xor_1 (C1_prime, C1, decoder_1_out2);
  xor xor_2 (C3_prime, decoder_1_out8, C3);
  xor xor_3 (Z0, D0, decoder_1_out3);
  xor xor_4 (Z1, D1, decoder_1_out5);
  xor xor_5 (Z2, D2, decoder_1_out6);
  xor xor_6 (Z3, D3, decoder_1_out7);
  xor xor_7 (Z4, D4, decoder_1_out9);
  xor xor_8 (Z5, D5, decoder_1_out10);
  xor xor_9 (Z6, D6, decoder_1_out11);
  xor xor_10 (Z7, D7, decoder_1_out12);
  xor xor_11 (Z8, D8, decoder_1_out13);
  xor xor_12 (Z9, D9, decoder_1_out14);
  // Probe on {1'b0, E, Z9, Z8}
  Counter #(.width(6), .max('h33), .ongoal("stay")) counter_1 (
    .Q(counter_1_q), .clk(CLK), .clr(reset));  // open: load, D, count, carry
  // Probe on {Z7, Z6, Z5, Z4}
  Multiplexer #(.select(2), .width(4), .disabled(0)) multiplexer_1 (
    .in0(4'b0000), .in1({1'b0, E, Z9, Z8}), .in2({Z7, Z6, Z5, Z4}), .in3({Z3, Z2, Z1, Z0}),
    .out(multiplexer_1_out), .sel(counter_1_q[1:0]));  // open: en
  not not_1 (go, counter_1_q[5]);
  Clock clock_1 (.out(clock_1_out));
  // Probe on {Z3, Z2, Z1, Z0}
  and and_1 (CLK, go, clock_1_out);
  xor xor_13 (C0_prime, C0, decoder_1_out1);
  xor xor_14 (C2_prime, C2, decoder_1_out4);
  TTY #(.cols(4)) tty_1 (.data({3'b100, multiplexer_1_out}), .clk(CLK), .we(go), .clr(reset));
  // Probe on {C5, D9, D8, D7, D6, D5, D4, C3, D3, D2, D1, C2, D0, C1, C0}
  ROM #(.addrWidth(3), .dataWidth(15)) rom_1 (
    .addr(counter_1_q[4:2]), .data({C5, D9, D8, D7, D6, D5, D4, C3, D3, D2, D1, C2, D0, C1, C0}));  // open: sel
  Button u_Reset (.out(reset));

  // Notes on the sheet:
  //   Press Reset and Ctrl-T or Ctrl-K
  //   Please set tick frequency to 2KHz
  //   @@NB
  //   @@KH
  //   @FLJ
  //   @CJA
  //   @@MK
  //   @GFK
  //   @CMC
  //   @@AK
  //   contents of rom_1 (hex, n*v repeats v):
  //   4e90 49c0 68d3 7a0c d5f 3457 3d95 4154
endmodule
