// Logisim project four.circ as structural Verilog: 1 circuit, main circuit main
module main (
);

  wire A_nBC_out, A_q, A_qn, AB_nC_nX_out, B_nC_nX_out, B_nC_out, B_q, B_qn, C_q, C_qn, clock_1_out,
       clock_2_out, clock_3_out, Go, nA_nB_nX_out, nA_nBX_out, nAB_out, nABD_out, nAC_out, nBCX_out,
       not_1_out, or_1_out, or_2_out, or_3_out, t_ff_1_q, t_ff_2_q, x, z;
  wire [1:0] counter_1_q;
  wire [4:0] counter_2_q;

  not not_1 (not_1_out, x);
  and nAB (nAB_out, A_qn, B_q);
  and B_nC (B_nC_out, B_q, C_qn, C_qn);
  and A_nBC (A_nBC_out, A_q, B_qn, C_q);
  and nAC (nAC_out, A_qn, C_q);
  and B_nC_nX (B_nC_nX_out, B_q, C_qn, not_1_out);
  and nBCX (nBCX_out, B_qn, C_q, x);
  and nA_nBX (nA_nBX_out, A_qn, B_qn, x);
  and nA_nB_nX (nA_nB_nX_out, A_qn, B_qn, not_1_out);
  and nABD (nABD_out, A_qn, B_q, x);
  and AB_nC_nX (AB_nC_nX_out, A_q, B_q, C_qn, not_1_out);
  or or_1 (or_1_out, B_nC_out, nAB_out, A_nBC_out);
  or or_2 (or_2_out, nAC_out, B_nC_nX_out, nBCX_out, nA_nBX_out);
  or or_3 (or_3_out, AB_nC_nX_out, nAC_out, nBCX_out, nA_nB_nX_out, nABD_out);
  Clock clock_1 (.out(clock_1_out));
  D_Flip_Flop A (.clk(clock_1_out), .D(or_1_out), .Q(A_q), .Qn(A_qn));  // open: preset, en, reset
  D_Flip_Flop B (.clk(clock_1_out), .D(or_2_out), .Q(B_q), .Qn(B_qn));  // open: preset, en, reset
  D_Flip_Flop C (.clk(clock_1_out), .D(or_3_out), .Q(C_q), .Qn(C_qn));  // open: preset, en, reset
  and and_1 (z, A_q, B_qn, C_qn, not_1_out);
  Clock clock_2 (.out(clock_2_out));
  TTY #(.rows(16), .cols(4)) tty_1 (.data({6'b011000, z}), .clk(clock_2_out), .we(Go));  // open: clr
  Counter #(.width(2), .max('h3)) counter_1 (.Q(counter_1_q), .clk(clock_2_out));  // open: load, D, count, carry, clr
  // Probe on counter_2_q
  Counter #(.width(5), .max('h1f), .ongoal("stay")) counter_2 (
    .Q(counter_2_q), .clk(t_ff_2_q));  // open: load, D, count, carry, clr
  T_Flip_Flop t_ff_1 (.clk(clock_3_out), .T(1'b1), .Q(t_ff_1_q));  // open: Qn, preset, reset, en
  Clock clock_3 (.out(clock_3_out));
  // Probe on x
  Multiplexer #(.select(2)) multiplexer_1 (
    .in0(counter_2_q[3]), .in1(counter_2_q[2]), .in2(counter_2_q[1]), .in3(counter_2_q[0]), .out(x),
    .sel(counter_1_q));  // open: en
  not not_2 (Go, counter_2_q[4]);
  T_Flip_Flop t_ff_2 (.clk(t_ff_1_q), .T(1'b1), .Q(t_ff_2_q));  // open: Qn, preset, reset, en
  TTY #(.rows(16), .cols(4)) tty_2 (.data({6'b011000, x}), .clk(clock_2_out), .we(Go));  // open: clr

  // Notes on the sheet:
  //   z
  //   Ctrl-r, then Ctrl-k.  Last line may be anything.
  //   0000
  //   0000
  //   0000
  //   0000
  //   0000
  //   0000
  //   0000
  //   0000
  //   0000
  //   0001
  //   0000
  //   0001
  //   0000
  //   0000
  //   0000
  //   ????
  //   x
endmodule
