// Logisim project parity.circ as structural Verilog: 1 circuit, main circuit main
module main (
);

  wire A, A_nBC_nD_out, A_nC_out, A_nD_out, A_prime, AB_nC_out, and_1_out, and_2_out, B, B_nC_out, B_nD_out,
       B_prime, BCD_out, C, C_nD_out, C_nE_out, C_prime, CDE_out, clock_1_out, clock_2_out, counter_1_carry,
       D, D_nE_out, D_prime, e, Go, nCDE_out, nDE_out, nE_out, not_1_out, not_3_out, not_4_out, or_1_out,
       or_3_out, or_4_out, or_5_out, x, y, z;

  not not_1 (not_1_out, e);
  and B_nC (B_nC_out, B, C_prime);
  and B_nD (B_nD_out, B, D_prime);
  and A_nC (A_nC_out, A, C_prime);
  and A_nD (A_nD_out, A, D_prime);
  and CDE (CDE_out, C, D, e);
  and C_nD (C_nD_out, C, D_prime, D_prime);
  and C_nE (C_nE_out, C, not_1_out);
  and nCDE (nCDE_out, C_prime, D, e);
  and nDE (nDE_out, D_prime, e);
  and D_nE (D_nE_out, D, not_1_out);
  buf nE (nE_out, not_1_out);  // AND_Gate
  and BCD (BCD_out, B, C, D);
  and AB_nC (AB_nC_out, A, B, C_prime);
  and A_nBC_nD (A_nBC_nD_out, A, B_prime, C, D_prime);
  or or_1 (or_1_out, nDE_out, D_nE_out);
  or or_2 (z, BCD_out, AB_nC_out, A_nBC_nD_out);
  Clock clock_1 (.out(clock_1_out));
  D_Flip_Flop u_A (.clk(clock_1_out), .D(or_3_out), .Q(A), .Qn(A_prime));  // open: preset, en, reset
  or or_3 (or_3_out, B_nC_out, B_nD_out, A_nC_out, A_nD_out, CDE_out);
  D_Flip_Flop u_B (.clk(clock_1_out), .D(or_4_out), .Q(B), .Qn(B_prime));  // open: preset, en, reset
  or or_4 (or_4_out, C_nD_out, C_nE_out, nCDE_out);
  D_Flip_Flop u_C (.clk(clock_1_out), .D(or_1_out), .Q(C), .Qn(C_prime));  // open: preset, en, reset
  D_Flip_Flop u_D (.clk(clock_1_out), .D(nE_out), .Q(D), .Qn(D_prime));  // open: preset, en, reset
  TTY #(.rows(32), .cols(1)) tty_1 (.data({6'b011000, z}), .clk(clock_2_out), .we(Go));  // open: clr
  Clock clock_2 (.out(clock_2_out));
  Random #(.width(2), .seed(2)) random_1 (.clk(clock_2_out), .next(Go), .out({y, x}));  // open: clr
  TTY #(.rows(32), .cols(1)) tty_2 (.data({6'b011000, x}), .clk(clock_2_out), .we(Go));  // open: clr
  TTY #(.rows(32), .cols(1)) tty_3 (.data({6'b011000, y}), .clk(clock_2_out), .we(Go));  // open: clr
  // Probe on x
  Counter #(.width(5), .max('h1f), .ongoal("stay")) counter_1 (
    .carry(counter_1_carry), .clk(clock_2_out));  // open: load, D, count, Q, clr
  not not_2 (Go, counter_1_carry);
  not not_3 (not_3_out, x);
  not not_4 (not_4_out, y);
  // Probe on y
  and and_1 (and_1_out, x, not_4_out);
  and and_2 (and_2_out, not_3_out, y);
  or or_5 (or_5_out, and_1_out, and_2_out);
  not not_5 (e, or_5_out);

  // Notes on the sheet:
  //   0
  //   0
  //   0
  //   1
  //   1
  //   1
  //   0
  //   1
  //   0
  //   0
  //   0
  //   1
  //   1
  //   1
  //   0
  //   1
  //   0
  //   0
  //   1
  //   0
  //   0
  //   0
  //   0
  //   1
  //   1
  //   0
  //   1
  //   1
  //   0
  //   0
  //   1
  //   Ctrl-r, then Ctrl-k
endmodule
