// Logisim project vending.circ as structural Verilog: 1 circuit, main circuit main
// F
module main (
);

  wire _30_Done, A, A_nBE_out, A_nBF_out, A_nD_nE_nF_out, A_prime, ABD_out, ABF_out, AD_out, AE_out,
       and_1_out, B, B_nCD_out, B_nD_nE_nF_out, B_prime, BCD_out, BCF_out, BD_out, C, C_nD_nE_nF_out,
       C_prime, CD_out, CF_out, CLK, clock_1_out, clock_2_out, clock_3_out, clock_4_out, clock_5_out,
       clock_6_out, counter_3_carry, d_ff_1_q, d_ff_2_q, Go, nA_nB_nCD_out, nA_nBE_out, nA_nCE_out,
       nA_nCF_out, nABE_out, nABF_out, nBCE_out, not_1_out, not_2_out, not_3_out, or_1_out, or_2_out,
       or_3_out, or_7_out, t_ff_1_q, x1, x2, x3, z1, z2, z3, z4;
  wire [1:0] counter_3_q;
  wire [2:0] counter_2_q;
  wire [3:0] rom_1_data, rom_1_data_2, rom_1_data_3, rom_1_data_4, rom_1_data_5, rom_1_data_6, rom_1_data_7,
       rom_1_data_8;
  wire [3:3] multiplexer_3_out;
  wire [5:0] counter_1_q;
  wire [6:0] multiplexer_1_out, multiplexer_2_out, xs;

  not not_1 (not_1_out, x1);
  not not_2 (not_2_out, x2);
  not not_3 (not_3_out, x3);
  and nABE (nABE_out, A_prime, B, x2);
  and BCF (BCF_out, C, B, x3);
  and ABF (ABF_out, A, B, x3);
  and nA_nB_nCD (nA_nB_nCD_out, A_prime, B_prime, C_prime, x1);
  and A_nD_nE_nF (A_nD_nE_nF_out, A, not_1_out, not_2_out, not_3_out);
  and CF (CF_out, C, x3);
  and nA_nBE (nA_nBE_out, A_prime, B_prime, x2);
  and nA_nCE (nA_nCE_out, A_prime, C_prime, x2);
  and nABF (nABF_out, A_prime, B, x3);
  and B_nD_nE_nF (B_nD_nE_nF_out, B, not_1_out, not_2_out, not_3_out);
  and nA_nCF (nA_nCF_out, A_prime, C_prime, x3);
  and nBCE (nBCE_out, B_prime, C, x2);
  and C_nD_nE_nF (C_nD_nE_nF_out, C, not_1_out, not_2_out, not_3_out);
  or or_1 (or_1_out, nABE_out, BCF_out, ABF_out, nA_nB_nCD_out, A_nD_nE_nF_out);
  and CD (CD_out, C, x1);
  and BD (BD_out, B, x1);
  and AE (AE_out, A, x2);
  and AD (AD_out, A, x1);
  and A_nBF (A_nBF_out, A, B_prime, x3);
  and B_nCD (B_nCD_out, B, C_prime, x1);
  and A_nBE (A_nBE_out, A, B_prime, x2);
  and BCD (BCD_out, B, C, x1);
  and ABD (ABD_out, A, B, x1);
  and A_nBD (z4, A, B_prime, x1);
  or or_2 (or_2_out, CF_out, nA_nBE_out, nA_nCE_out, nABF_out, B_nD_nE_nF_out);
  or or_3 (or_3_out, nA_nCF_out, nBCE_out, C_nD_nE_nF_out);
  or or_4 (z1, CD_out, BD_out, AE_out, AD_out, A_nBF_out);
  or or_5 (z2, B_nCD_out, A_nBE_out);
  or or_6 (z3, BCD_out, ABD_out);
  D_Flip_Flop u_A (.clk(CLK), .D(or_1_out), .Q(A), .Qn(A_prime));  // open: preset, en, reset
  D_Flip_Flop u_B (.clk(CLK), .D(or_2_out), .Q(B), .Qn(B_prime));  // open: preset, en, reset
  D_Flip_Flop u_C (.clk(CLK), .D(or_3_out), .Q(C), .Qn(C_prime));  // open: preset, en, reset
  // Probe on counter_1_q
  Counter #(.width(6), .max('h3f)) counter_1 (
    .count(_30_Done), .Q(counter_1_q), .clk(and_1_out));  // open: load, D, carry, clr
  and and_1 (and_1_out, clock_1_out, Go);
  Clock clock_1 (.out(clock_1_out));
  Clock clock_2 (.out(clock_2_out));
  nand _37_Stop (Go, counter_1_q[5], counter_1_q[2], counter_1_q[0]);
  // Probe on {3'b011, z1, z2, z3, z4}
  Multiplexer #(.width(7)) multiplexer_1 (
    .in0({3'b011, z1, z2, z3, z4}), .in1(7'b0001010), .out(multiplexer_1_out), .sel(_30_Done));  // open: en
  // Probe on multiplexer_1_out
  or or_7 (or_7_out, CLK, d_ff_1_q);
  D_Flip_Flop d_ff_1 (.clk(clock_2_out), .D(_30_Done), .Q(d_ff_1_q));  // open: Qn, preset, en, reset
  TTY #(.rows(38), .cols(7)) tty_1 (.data(multiplexer_1_out), .clk(or_7_out), .we(Go));  // open: clr
  ROM #(.addrWidth(6), .dataWidth(32)) rom_1 (
    .addr(counter_1_q),
    .data({rom_1_data_8, rom_1_data_6, rom_1_data_7, rom_1_data_5, rom_1_data_4, rom_1_data_3, rom_1_data_2, rom_1_data}));  // open: sel
  TTY #(.rows(38), .cols(25)) tty_2 (.data(multiplexer_2_out), .clk(clock_3_out), .we(Go));  // open: clr
  Clock clock_3 (.out(clock_3_out));
  // Probe on multiplexer_2_out
  Multiplexer #(.width(7)) multiplexer_2 (
    .in0(xs), .in1(7'b0001010), .out(multiplexer_2_out), .sel(_30_Done));  // open: en
  Counter #(.width(3), .max('h7)) counter_2 (
    .Q(counter_2_q), .clk(counter_3_carry), .clr(d_ff_2_q));  // open: load, D, count, carry
  Clock clock_4 (.out(clock_4_out));
  T_Flip_Flop t_ff_1 (.clk(clock_5_out), .T(1'b1), .Q(t_ff_1_q));  // open: Qn, preset, reset, en
  Clock clock_5 (.out(clock_5_out));
  // Probe on {multiplexer_3_out[3], x1, x2, x3}
  Multiplexer #(.select(3), .width(4)) multiplexer_3 (
    .in0(rom_1_data_8), .in1(rom_1_data_6), .in2(rom_1_data_7), .in3(rom_1_data_5), .in4(rom_1_data_4),
    .in5(rom_1_data_3), .in6(rom_1_data_2), .out({multiplexer_3_out[3], x1, x2, x3}), .sel(counter_2_q));  // open: in7, en
  // Probe on counter_2_q
  D_Flip_Flop d_ff_2 (.clk(clock_4_out), .D(_30_Done), .Q(d_ff_2_q));  // open: Qn, preset, en, reset
  T_Flip_Flop t_ff_2 (.clk(t_ff_1_q), .T(1'b1), .Q(CLK));  // open: Qn, preset, reset, en
  nor nor_1 (_30_Done, x1, x2, x3);
  Multiplexer #(.select(2), .width(7)) multiplexer_4 (
    .in0({6'b011000, x1}), .in1({6'b011000, x2}), .in2({6'b011000, x3}), .in3(7'b0100000), .out(xs),
    .sel(counter_3_q));  // open: en
  // Probe on counter_3_q
  Counter #(.width(2), .max('h3)) counter_3 (
    .Q(counter_3_q), .carry(counter_3_carry), .clk(clock_6_out), .clr(_30_Done));  // open: load, D, count
  Clock clock_6 (.out(clock_6_out));
  // Probe on xs

  // Notes on the sheet:
  //   D
  //   E
  //   F
  //   D
  //   E
  //   F
  //   Output
  //   contents of rom_1 (hex, n*v repeats v):
  //   11111100 11111200 11111400 11121000 11122000 11124000 11211000 11212000 11214000 12111000 12112000
  //   12114000 12210000 12220000 12240000 21111000 21210000 21220000 21240000 22110000 22120000 22140000
  //   11112000 11114000 11220000 11240000 21120000 21140000 22200000 22400000 11140000 12400000 21400000
  //   11400000 24000000 14000000
  //   You must use the CLK tunnel for your clock source.  Ctrl-r, then Ctrl-k to test.
  //   000008
  //   00000<
  //   000009
  //   00008
  //   0000<
  //   00009
  //   00008
  //   0000<
  //   00009
  //   00008
  //   0000<
  //   00009
  //   0008
  //   000<
  //   0009
  //   00008
  //   0008
  //   000<
  //   0009
  //   0008
  //   000<
  //   0009
  //   00008
  //   0000>
  //   0008
  //   000>
  //   0008
  //   000>
  //   008
  //   00>
  //   000:
  //   00:
  //   00:
  //   00<
  //   0<
  //   08
  //   Input
endmodule
