// Logisim project CPU.circ as structural Verilog: 10 circuits, main circuit main
module main (
  output [9:0] out_1,
  output [9:0] out_2,
  output [9:0] out_3,
  output [9:0] out_4,
  output [9:0] out_5,
  output [9:0] out_6,
  output [9:0] out_7,
  output ignore,
  output halt
);

  wire _0, _1, _2, _3, _4, _5, _6, _7, _8, _9, addl, and_1_out, benz, CLK, clock_1_out, comparator_1_lt,
       comparator_2_lt, decoder_1_out0, decoder_1_out1, decoder_1_out2, decoder_1_out3, decoder_1_out4,
       decoder_1_out5, decoder_1_out6, enable, movl, not_1_out, or_1_out, pc1, pc2, pc3, pc4, pc5, stop,
       subl, t_ff_1_q, TClock;
  wire [1:0] counter_2_q, Upper_2_bits;
  wire [2:0] A, B, Dest, rom_1_data;
  wire [3:0] ALU;
  wire [4:0] counter_1_q, multiplexer_1_out, programcounter_1_out_8;
  wire [6:0] adder_2_out, adder_3_out, ASCII, LSB, MiddleBits;
  wire [7:0] multiplexer_2_out;
  wire [9:0] Data, multiplexer_4_out, multiplexer_7_out, multiplexer_8_out, multiplexer_9_out;
  wire [23:23] ram_1_data;

  ProgramCounter programcounter_1 (
    .in_3(pc1), .in_4(pc2), .in_5(pc3), .in_6(pc4), .in_7(pc5), .out_8(programcounter_1_out_8), .in_1(CLK),
    .in_2(1'b1));
  adder adder_1 (
    ._0(1'b0), .C0(pc1), .C2(pc3), .C1(pc2), .C4(pc4), .C5(pc5), .A0(programcounter_1_out_8[0]),
    .A1(programcounter_1_out_8[1]), .A2(programcounter_1_out_8[2]), .A3(programcounter_1_out_8[3]),
    .A4(programcounter_1_out_8[4]), .B0(multiplexer_1_out[0]), .B1(multiplexer_1_out[1]),
    .B2(multiplexer_1_out[2]), .B3(multiplexer_1_out[3]), .B4(multiplexer_1_out[4]));  // open: C6
  RAM #(.addrWidth(5), .dataWidth(24)) ram_1 (
    .addr(programcounter_1_out_8), .data({ram_1_data[23], ALU, Dest, A, B, Data}), .clk(CLK));  // open: sel, ld, clr
  TTY #(.rows(33), .cols(4)) tty_1 (.data(ASCII), .clk(TClock));  // open: we, clr
  Multiplexer #(.width(5)) multiplexer_1 (
    .in0(5'b00001), .in1(Data[4:0]), .out(multiplexer_1_out), .sel(benz), .en(stop));
  // Probe on out_1
  // Probe on out_5
  Counter #(.width(5), .max('h1f), .ongoal("stay")) counter_1 (
    .Q(counter_1_q), .carry(halt), .clk(CLK));  // open: load, D, count, clr
  // Probe on out_2
  // Probe on out_6
  Multiplexer #(.select(3), .width(10)) multiplexer_2 (
    .in0(out_1), .in1(out_2), .in2(out_3), .in3(out_4), .in4(out_5), .in5(out_6), .in6(out_7),
    .out({Upper_2_bits, multiplexer_2_out}), .sel(rom_1_data));  // open: in7, en
  not not_1 (not_1_out, halt);
  Clock clock_1 (.out(clock_1_out));
  immediate immediate_1 (
    .in_1(ram_1_data[23]), .in_2(ALU[3]), .in_3(ALU[2]), .in_4(ALU[1]), .in_5(ALU[0]), .enable(enable),
    .stop(stop), .enable_2(enable), .addl(addl), .subl(subl), .movl(movl), .benz(benz), .enable_3(enable));
  ROM #(.addrWidth(5), .dataWidth(3)) rom_1 (.addr(counter_1_q), .data(rom_1_data));  // open: sel
  and and_1 (and_1_out, not_1_out, clock_1_out);
  not not_2 (TClock, and_1_out);
  // Probe on out_3
  // Probe on out_7
  // Probe on out_4
  Comparator #(.width(7)) comparator_1 (
    .a(7'b0111001), .b({3'b011, multiplexer_2_out[3:0]}), .lt(comparator_1_lt));  // open: gt, eq
  Comparator #(.width(7)) comparator_2 (
    .a(7'b0111001), .b({3'b011, multiplexer_2_out[7:4]}), .lt(comparator_2_lt));  // open: gt, eq
  T_Flip_Flop t_ff_1 (.clk(and_1_out), .T(1'b1), .Q(t_ff_1_q));  // open: Qn, preset, reset, en
  T_Flip_Flop t_ff_2 (.clk(t_ff_1_q), .T(1'b1), .Q(CLK));  // open: Qn, preset, reset, en
  Adder #(.width(7)) adder_2 (
    .a({3'b011, multiplexer_2_out[3:0]}), .b(7'b0000111), .out(adder_2_out));  // open: cin, cout
  Adder #(.width(7)) adder_3 (
    .a({3'b011, multiplexer_2_out[7:4]}), .b(7'b0000111), .out(adder_3_out));  // open: cin, cout
  Multiplexer #(.select(2), .width(7)) multiplexer_3 (
    .in0({5'b01100, Upper_2_bits}), .in1(MiddleBits), .in2(LSB), .in3(7'b0100000), .out(ASCII),
    .sel(counter_2_q));  // open: en
  Counter #(.width(2), .max('h3)) counter_2 (.Q(counter_2_q), .clk(TClock));  // open: load, D, count, carry, clr
  Decoder #(.select(3)) decoder_1 (
    .out0(decoder_1_out0), .out1(decoder_1_out1), .out2(decoder_1_out2), .out3(decoder_1_out3),
    .out4(decoder_1_out4), .out5(decoder_1_out5), .out6(decoder_1_out6), .sel(Dest), .en(enable));  // open: out7
  RegBank regbank_1 (
    .R2_2(out_3), .R0_2(out_1), .R1_2(out_2), .R6_2(out_7), .R5_2(out_6), .R3_2(out_4), .R4_2(out_5),
    .CLK(CLK), .A0(_0), .A1(_1), .A2(_2), .A3(_3), .A4(_4), .A5(_5), .A6(_6), .A7(_7), .A8(_8), .A9(_9),
    .R0(decoder_1_out0), .R1(decoder_1_out1), .R2(decoder_1_out2), .R3(decoder_1_out3), .R4(decoder_1_out4),
    .R5(decoder_1_out5), .R6(decoder_1_out6));
  Multiplexer #(.select(3), .width(10)) multiplexer_4 (
    .in0(out_1), .in1(out_2), .in2(out_3), .in3(out_4), .in4(out_5), .in5(out_6), .in6(out_7),
    .out(multiplexer_4_out), .sel(Dest));  // open: in7, en
  Multiplexer #(.width(7), .disabled(0), .enable("false")) multiplexer_5 (
    .in0({3'b011, multiplexer_2_out[3:0]}), .in1(adder_2_out), .out(LSB), .sel(comparator_1_lt));
  Multiplexer #(.width(7), .disabled(0), .enable("false")) multiplexer_6 (
    .in0({3'b011, multiplexer_2_out[7:4]}), .in1(adder_3_out), .out(MiddleBits), .sel(comparator_2_lt));
  compare compare_1 (
    .in_11(ALU), .A0(multiplexer_4_out[9]), .A1(multiplexer_4_out[8]), .A2(multiplexer_4_out[7]),
    .A3(multiplexer_4_out[6]), .A4(multiplexer_4_out[5]), .A5(multiplexer_4_out[4]),
    .A6(multiplexer_4_out[3]), .A7(multiplexer_4_out[2]), .A8(multiplexer_4_out[1]),
    .A9(multiplexer_4_out[0]), .out_12(stop));
  T_Flip_Flop t_ff_3 (.clk(CLK), .T(1'b1), .Q(ignore));  // open: Qn, preset, reset, en
  Multiplexer #(.select(3), .width(10)) multiplexer_7 (
    .in0(out_1), .in1(out_2), .in2(out_3), .in3(out_4), .in4(out_5), .in5(out_6), .in6(out_7),
    .out(multiplexer_7_out), .sel(A), .en(enable));  // open: in7
  or or_1 (or_1_out, addl, subl, movl, benz);
  ALU alu_1 (
    .out_22({_9, _8, _7, _6, _5, _4, _3, _2, _1, _0}), .A0(multiplexer_7_out[0]), .A1(multiplexer_7_out[1]),
    .A2(multiplexer_7_out[2]), .A3(multiplexer_7_out[3]), .A4(multiplexer_7_out[4]),
    .A5(multiplexer_7_out[5]), .A6(multiplexer_7_out[6]), .A7(multiplexer_7_out[7]),
    .B0(multiplexer_9_out[0]), .B1(multiplexer_9_out[1]), .B2(multiplexer_9_out[2]),
    .B3(multiplexer_9_out[3]), .B4(multiplexer_9_out[4]), .B5(multiplexer_9_out[5]),
    .B7(multiplexer_9_out[7]), .A8(multiplexer_7_out[8]), .A9(multiplexer_7_out[9]),
    .B8(multiplexer_9_out[8]), .B9(multiplexer_9_out[9]), .ALU(ALU), .B6(multiplexer_9_out[6]));
  Multiplexer #(.select(3), .width(10)) multiplexer_8 (
    .in0(out_1), .in1(out_2), .in2(out_3), .in3(out_4), .in4(out_5), .in5(out_6), .in6(out_7),
    .out(multiplexer_8_out), .sel(B), .en(enable));  // open: in7
  Multiplexer #(.width(10)) multiplexer_9 (
    .in0(multiplexer_8_out), .in1(Data), .out(multiplexer_9_out), .sel(or_1_out), .en(enable));

  // Other names for the same wires on the sheet: R0[9:0] = out_1; R1[9:0] = out_2; R2[9:0] = out_3; R3[9:0] = out_4;
  //   R4[9:0] = out_5; R5[9:0] = out_6; R6[9:0] = out_7

  // Notes on the sheet:
  //   DO NOT PUT ANY PINS ON THE main circuit.  (You should not need any anyway.)
  //   0F5
  //   0F5
  //   25A
  //   050
  //   2FF
  //   30A
  //   34F
  //   0F5
  //   1EA
  //   07A
  //   29B
  //   165
  //   10F
  //   0F5
  //   0AA
  //   0AA
  //   05A
  //   00A
  //   0FA
  //   104
  //   0B4
  //   165
  //   165
  //   001
  //   001
  //   000
  //   000
  //   000
  //   000
  //   000
  //   ???
  //   There is no Reset.  Just Ctrl-r, then load test.txt into your RAM, and then Ctrl-k
  //   You must  use the CLK tunnel for the source of your clock.  R0-R6 are the other tunnels you need to connect
  //   contents of rom_1 (hex, n*v repeats v):
  //   0 0 0 1 2 3 4 5 6 2 3 4 5 6 0 0 0 1 3 4 6 3 5 5 8*6
endmodule

module REGISTER (
  input  in_1,
  input  in_2,
  input  in_3,
  input  in_4,
  input  in_5,
  input  in_6,
  input  in_7,
  input  in_8,
  input  in_9,
  input  in_10,
  input  in_11,
  input  in_12,
  output [9:0] out_13
);

  D_Flip_Flop FF0 (.clk(in_1), .D(in_3), .Q(out_13[0]), .en(in_2));  // open: Qn, preset, reset
  D_Flip_Flop FF1 (.clk(in_1), .D(in_4), .Q(out_13[1]), .en(in_2));  // open: Qn, preset, reset
  D_Flip_Flop FF2 (.clk(in_1), .D(in_5), .Q(out_13[2]), .en(in_2));  // open: Qn, preset, reset
  D_Flip_Flop FF3 (.clk(in_1), .D(in_6), .Q(out_13[3]), .en(in_2));  // open: Qn, preset, reset
  D_Flip_Flop FF4 (.clk(in_1), .D(in_7), .Q(out_13[4]), .en(in_2));  // open: Qn, preset, reset
  D_Flip_Flop FF5 (.clk(in_1), .D(in_8), .Q(out_13[5]), .en(in_2));  // open: Qn, preset, reset
  D_Flip_Flop FF6 (.clk(in_1), .D(in_9), .Q(out_13[6]), .en(in_2));  // open: Qn, preset, reset
  D_Flip_Flop FF7 (.clk(in_1), .D(in_10), .Q(out_13[7]), .en(in_2));  // open: Qn, preset, reset
  D_Flip_Flop FF8 (.clk(in_1), .D(in_11), .Q(out_13[8]), .en(in_2));  // open: Qn, preset, reset
  D_Flip_Flop FF9 (.clk(in_1), .D(in_12), .Q(out_13[9]), .en(in_2));  // open: Qn, preset, reset
endmodule

module ALU (
  input  [3:0] ALU,
  input  A0,
  input  A1,
  input  A2,
  input  A3,
  input  A4,
  input  A5,
  input  A6,
  input  A7,
  input  A8,
  input  A9,
  input  B0,
  input  B1,
  input  B2,
  input  B3,
  input  B4,
  input  B5,
  input  B6,
  input  B7,
  input  B8,
  input  B9,
  output [9:0] out_22
);

  wire BI0, BI1, BI2, BI3, BI4, BI5, BI6, BI7, BI8, BI9, CARRYOUT0, CARRYOUT1, CARRYOUT2, CARRYOUT3,
       CARRYOUT4, CARRYOUT5, CARRYOUT6, CARRYOUT7, CARRYOUT8, CARRYOUT9, CARRYOUTI0, CARRYOUTI1, CARRYOUTI2,
       CARRYOUTI3, CARRYOUTI4, CARRYOUTI5, CARRYOUTI6, CARRYOUTI7, CARRYOUTI8, CARRYOUTI9;

  subALU subalu_1 (
    .A(A0), .B(B0), .Cin(1'b0), .SHL(1'b0), .SHR(A1), .BI(BI0), .CinI(1'b1), .SUM(out_22[0]),
    .CARRYOUT(CARRYOUT0), .CARRYOUTI(CARRYOUTI0), .in_6(ALU));
  subALU subalu_2 (
    .A(A1), .B(B1), .Cin(CARRYOUT0), .SHL(A0), .SHR(A2), .BI(BI1), .CinI(CARRYOUTI0), .SUM(out_22[1]),
    .CARRYOUT(CARRYOUT1), .CARRYOUTI(CARRYOUTI1), .in_6(ALU));
  subALU subalu_3 (
    .A(A2), .B(B2), .Cin(CARRYOUT1), .SHL(A1), .SHR(A3), .BI(BI2), .CinI(CARRYOUTI1), .SUM(out_22[2]),
    .CARRYOUT(CARRYOUT2), .CARRYOUTI(CARRYOUTI2), .in_6(ALU));
  subALU subalu_4 (
    .A(A3), .B(B3), .Cin(CARRYOUT2), .SHL(A2), .SHR(A4), .BI(BI3), .CinI(CARRYOUTI2), .SUM(out_22[3]),
    .CARRYOUT(CARRYOUT3), .CARRYOUTI(CARRYOUTI3), .in_6(ALU));
  subALU subalu_5 (
    .A(A4), .B(B4), .Cin(CARRYOUT3), .SHL(A3), .SHR(A5), .BI(BI4), .CinI(CARRYOUTI3), .SUM(out_22[4]),
    .CARRYOUT(CARRYOUT4), .CARRYOUTI(CARRYOUTI4), .in_6(ALU));
  subALU subalu_6 (
    .A(A5), .B(B5), .Cin(CARRYOUT4), .SHL(A4), .SHR(A6), .BI(BI5), .CinI(CARRYOUTI4), .SUM(out_22[5]),
    .CARRYOUT(CARRYOUT5), .CARRYOUTI(CARRYOUTI5), .in_6(ALU));
  subALU subalu_7 (
    .A(A6), .B(B6), .Cin(CARRYOUT5), .SHL(A5), .SHR(A7), .BI(BI6), .CinI(CARRYOUTI5), .SUM(out_22[6]),
    .CARRYOUT(CARRYOUT6), .CARRYOUTI(CARRYOUTI6), .in_6(ALU));
  subALU subalu_8 (
    .A(A7), .B(B7), .Cin(CARRYOUT6), .SHL(A6), .SHR(A8), .BI(BI7), .CinI(CARRYOUTI6), .SUM(out_22[7]),
    .CARRYOUT(CARRYOUT7), .CARRYOUTI(CARRYOUTI7), .in_6(ALU));
  subALU subalu_9 (
    .A(A8), .B(B8), .Cin(CARRYOUT7), .SHL(A7), .SHR(A9), .BI(BI8), .CinI(CARRYOUTI7), .SUM(out_22[8]),
    .CARRYOUT(CARRYOUT8), .CARRYOUTI(CARRYOUTI8), .in_6(ALU));
  subALU subalu_10 (
    .A(A9), .B(B9), .Cin(CARRYOUT8), .SHL(A8), .SHR(1'b0), .BI(BI9), .CinI(CARRYOUTI8), .SUM(out_22[9]),
    .CARRYOUT(CARRYOUT9), .CARRYOUTI(CARRYOUTI9), .in_6(ALU));
  not not_1 (BI0, B0);
  not not_2 (BI1, B1);
  not not_3 (BI2, B2);
  not not_4 (BI3, B3);
  not not_5 (BI4, B4);
  not not_6 (BI5, B5);
  not not_7 (BI6, B6);
  not not_8 (BI7, B7);
  not not_9 (BI8, B8);
  not not_10 (BI9, B9);

  // Other names for the same wires on the sheet: output0 = out_22[0]; output1 = out_22[1]; output2 = out_22[2];
  //   output3 = out_22[3]; output4 = out_22[4]; output5 = out_22[5]; output6 = out_22[6]; output7 = out_22[7];
  //   output8 = out_22[8]; output9 = out_22[9]
endmodule

// ControlUnit
module immediate (
  input  in_1,
  input  in_2,
  input  in_3,
  input  in_4,
  input  in_5,
  output enable,
  output stop,
  output enable_2,
  output addl,
  output subl,
  output movl,
  output benz,
  output enable_3
);

  wire HALT_out, NOP_out, not_1_out, not_2_out, not_3_out, not_4_out, not_5_out;

  not not_1 (not_1_out, in_1);
  not not_2 (not_2_out, in_2);
  not not_3 (not_3_out, in_3);
  not not_4 (not_4_out, in_4);
  not not_5 (not_5_out, in_5);
  not not_6 (enable, HALT_out);
  and HALT (HALT_out, in_1, in_2, in_3, in_4, in_5);
  not not_7 (stop, HALT_out);
  not not_8 (enable_2, NOP_out);
  and NOP (NOP_out, not_1_out, in_2, in_3, not_4_out, not_5_out);
  and ADDI (addl, not_1_out, in_2, not_3_out, not_4_out, not_5_out);
  and SUBI (subl, not_1_out, in_2, not_3_out, not_4_out, in_5);
  and MOVI (movl, not_1_out, in_2, not_3_out, in_4, not_5_out);
  and u_BENZ (benz, not_1_out, in_2, not_3_out, in_4, in_5);
  not not_9 (enable_3, benz);
endmodule

// ADDER
module adder (
  input  A0,
  input  A1,
  input  A2,
  input  A3,
  input  A4,
  input  B0,
  input  B1,
  input  B2,
  input  B3,
  input  B4,
  input  _0,
  output C0,
  output C2,
  output C1,
  output C4,
  output C5,
  output C6
);

  wire D0, D1, D2, D3;

  adderhelper adderhelper_1 (.A(A0), .B(B0), .Cin(_0), .out_4(C0), .out_5(D0));
  adderhelper adderhelper_2 (.A(A1), .B(B1), .Cin(D0), .out_4(C1), .out_5(D1));
  adderhelper adderhelper_3 (.A(A2), .B(B2), .Cin(D1), .out_4(C2), .out_5(D2));
  adderhelper adderhelper_4 (.A(A3), .B(B3), .Cin(D2), .out_4(C4), .out_5(D3));
  adderhelper adderhelper_5 (.A(A4), .B(B4), .Cin(D3), .out_4(C5), .out_5(C6));
endmodule

module adderhelper (
  input  A,
  input  B,
  input  Cin,
  output out_4,
  output out_5
);

  wire and_1_out, and_2_out, and_3_out, and_4_out, and_5_out, not_1_out, not_2_out, or_1_out, or_2_out;

  and and_1 (and_1_out, A, B);
  and and_2 (and_2_out, A, B);
  not not_1 (not_1_out, and_1_out);
  or or_1 (or_1_out, A, B);
  and and_3 (and_3_out, not_1_out, or_1_out);
  and and_4 (and_4_out, and_3_out, Cin);
  and and_5 (and_5_out, and_3_out, Cin);
  not not_2 (not_2_out, and_5_out);
  or or_2 (or_2_out, Cin, and_3_out);
  or or_3 (out_5, and_4_out, and_2_out);
  and and_6 (out_4, not_2_out, or_2_out);
endmodule

module ProgramCounter (
  input  in_1,
  input  in_2,
  input  in_3,
  input  in_4,
  input  in_5,
  input  in_6,
  input  in_7,
  output [4:0] out_8
);

  D_Flip_Flop FF0 (.clk(in_1), .D(in_3), .Q(out_8[0]), .en(in_2));  // open: Qn, preset, reset
  D_Flip_Flop FF1 (.clk(in_1), .D(in_4), .Q(out_8[1]), .en(in_2));  // open: Qn, preset, reset
  D_Flip_Flop FF2 (.clk(in_1), .D(in_5), .Q(out_8[2]), .en(in_2));  // open: Qn, preset, reset
  D_Flip_Flop FF3 (.clk(in_1), .D(in_6), .Q(out_8[3]), .en(in_2));  // open: Qn, preset, reset
  D_Flip_Flop FF4 (.clk(in_1), .D(in_7), .Q(out_8[4]), .en(in_2));  // open: Qn, preset, reset
endmodule

// BENZ
module compare (
  input  A0,
  input  A1,
  input  A2,
  input  A3,
  input  A4,
  input  A5,
  input  A6,
  input  A7,
  input  A8,
  input  A9,
  input  [3:0] in_11,
  output out_12
);

  wire or_1_out, or_2_out, or_3_out, or_4_out, or_5_out, or_6_out, or_7_out, or_8_out, or_9_out, or_10_out,
       or_11_out;

  or or_1 (or_1_out, A0, 1'b0);
  or or_2 (or_2_out, A1, 1'b0);
  or or_3 (or_3_out, A2, 1'b0);
  or or_4 (or_4_out, A3, 1'b0);
  or or_5 (or_5_out, A4, 1'b0);
  or or_6 (or_6_out, A5, 1'b0);
  or or_7 (or_7_out, A6, 1'b0);
  or or_8 (or_8_out, A7, 1'b0);
  or or_9 (or_9_out, A8, 1'b0);
  or or_10 (or_10_out, A9, 1'b0);
  or or_11 (or_11_out, or_1_out, or_2_out, or_3_out, or_4_out, or_5_out, or_6_out, or_7_out, or_8_out, or_9_out, or_10_out);
  Multiplexer #(.select(4)) multiplexer_1 (
    .in0(1'b1), .in1(1'b1), .in2(1'b1), .in3(1'b1), .in4(1'b1), .in5(1'b1), .in6(1'b1), .in7(1'b1),
    .in8(1'b1), .in9(1'b1), .in10(1'b1), .in11(or_11_out), .out(out_12), .sel(in_11));  // open: in12, in13, in14, in15, en
endmodule

module RegBank (
  input  CLK,
  input  A0,
  input  A1,
  input  A2,
  input  A3,
  input  A4,
  input  A5,
  input  A6,
  input  A7,
  input  A8,
  input  A9,
  input  R0,
  input  R1,
  input  R2,
  input  R3,
  input  R4,
  input  R5,
  input  R6,
  output [9:0] R2_2,
  output [9:0] R0_2,
  output [9:0] R1_2,
  output [9:0] R6_2,
  output [9:0] R5_2,
  output [9:0] R3_2,
  output [9:0] R4_2
);

  REGISTER register_1 (
    .in_3(A0), .in_4(A1), .in_5(A2), .in_6(A3), .out_13(R0_2), .in_1(CLK), .in_2(R0), .in_7(A4), .in_8(A5),
    .in_9(A6), .in_10(A7), .in_11(A8), .in_12(A9));
  REGISTER register_2 (
    .in_3(A0), .in_4(A1), .in_5(A2), .in_6(A3), .out_13(R3_2), .in_1(CLK), .in_2(R3), .in_7(A4), .in_8(A5),
    .in_9(A6), .in_10(A7), .in_11(A8), .in_12(A9));
  REGISTER register_3 (
    .in_3(A0), .in_4(A1), .in_5(A2), .in_6(A3), .out_13(R1_2), .in_1(CLK), .in_2(R1), .in_7(A4), .in_8(A5),
    .in_9(A6), .in_10(A7), .in_11(A8), .in_12(A9));
  REGISTER register_4 (
    .in_3(A0), .in_4(A1), .in_5(A2), .in_6(A3), .out_13(R4_2), .in_1(CLK), .in_2(R4), .in_7(A4), .in_8(A5),
    .in_9(A6), .in_10(A7), .in_11(A8), .in_12(A9));
  REGISTER register_5 (
    .in_3(A0), .in_4(A1), .in_5(A2), .in_6(A3), .out_13(R2_2), .in_1(CLK), .in_2(R2), .in_7(A4), .in_8(A5),
    .in_9(A6), .in_10(A7), .in_11(A8), .in_12(A9));
  REGISTER register_6 (
    .in_3(A0), .in_4(A1), .in_5(A2), .in_6(A3), .out_13(R5_2), .in_1(CLK), .in_2(R5), .in_7(A4), .in_8(A5),
    .in_9(A6), .in_10(A7), .in_11(A8), .in_12(A9));
  REGISTER register_7 (
    .in_3(A0), .in_4(A1), .in_5(A2), .in_6(A3), .out_13(R6_2), .in_1(CLK), .in_2(R6), .in_7(A4), .in_8(A5),
    .in_9(A6), .in_10(A7), .in_11(A8), .in_12(A9));

  // Other names for the same wires on the sheet: _0 = A0; _1 = A1; _2 = A2; _3 = A3; _4 = A4; _5 = A5; _6 = A6;
  //   _7 = A7; _8 = A8; _9 = A9
endmodule

module subALU (
  input  A,
  input  B,
  input  Cin,
  input  SHL,
  input  SHR,
  input  [3:0] in_6,
  input  BI,
  input  CinI,
  output SUM,
  output CARRYOUT,
  output CARRYOUTI
);

  wire adderhelper_1_out_4, adderhelper_2_out_4, and_1_out, not_1_out, or_1_out;

  adderhelper adderhelper_1 (.A(A), .B(B), .Cin(Cin), .out_4(adderhelper_1_out_4), .out_5(CARRYOUT));
  adderhelper adderhelper_2 (.A(A), .B(BI), .Cin(CinI), .out_4(adderhelper_2_out_4), .out_5(CARRYOUTI));
  not not_1 (not_1_out, A);
  and and_1 (and_1_out, A, B);
  or or_1 (or_1_out, A, B);
  Multiplexer #(.select(4)) multiplexer_1 (
    .in0(and_1_out), .in1(or_1_out), .in2(not_1_out), .in3(adderhelper_1_out_4), .in4(A), .in5(SHL),
    .in6(SHR), .in7(adderhelper_2_out_4), .in8(adderhelper_1_out_4), .in9(adderhelper_2_out_4), .in10(B),
    .in11(B), .out(SUM), .sel(in_6));  // open: in12, in13, in14, in15, en
endmodule
